# Fritzing sketch bigmclighting (saved by Fritzing 0.9.3b)

parts:
  WeMos_D1_Mini1 = WeMos D1 Mini
  5V_1_2A = Power plug
  12_x = Neopixel Strip -- Black (60/m) [part_number="SK6812 (RGBNW)"]
  Microswitch_6x6x13mm = Tactile Switch Buttons - 12mm Square [package=tactile-pth-12mm]
  TSOP_38238_(optional) = TSOP312.., 314.. [package=THT]

nets:
  N1: WeMos_D1_Mini1.3V3, TSOP_38238_(optional).Vs
  5V: WeMos_D1_Mini1.5V, 5V_1_2A.VCC, 12_x.+5V
  N2: WeMos_D1_Mini1.D5, Microswitch_6x6x13mm.2, Microswitch_6x6x13mm.4
  N3: WeMos_D1_Mini1.D7, TSOP_38238_(optional).Data
  GND: WeMos_D1_Mini1.G, 5V_1_2A.GND, 12_x.GND, Microswitch_6x6x13mm.1, Microswitch_6x6x13mm.3, TSOP_38238_(optional).GND
  N4: WeMos_D1_Mini1.RX, 12_x.DI

custom parts:
  WeMos D1 Mini: The D1 mini is a mini wifi board based on ESP-8266EX.
  Neopixel Strip -- Black (60/m): Neopixel Strip, Black, 60 pixels per meter.
  Tactile Switch Buttons - 12mm Square: Medium-sized clicky momentary switches are standard input "buttons" on electronic projects. These work best in a PCB but can be used on a solderless breadboard as shown in this tutorial. The pins are normally open (disconnected) and when the button is pressed they are momentarily closed. They come in a pack of 10, they're pretty handy so you'll want to keep them around. You can find an EAGLE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
